// Logisim project Decoder.circ as structural Verilog: 2 circuits, main circuit main
module main (
  input  in_1,
  input  in_2,
  input  in_3,
  output out_4,
  output out_5,
  output out_6,
  output out_7,
  output out_8,
  output out_9,
  output out_10,
  output out_11,
  output out_12,
  output out_13,
  output out_14,
  output out_15
);

  wire clock_1_out;
  wire [31:0] adder_1_out, register_1_q;
  wire [31:6] rom_1_data;

  Register #(.width(32)) register_1 (.D(adder_1_out), .en(in_1), .Q(register_1_q), .clk(clock_1_out), .clr(in_2));
  Clock clock_1 (.out(clock_1_out));
  // Probe on register_1_q
  Adder #(.width(32)) adder_1 (.a(register_1_q), .b(32'h4), .out(adder_1_out));  // open: cin, cout
  // Probe on {rom_1_data, {6{rom_1_data[6]}}}
  ROM #(.addrWidth(24), .dataWidth(32)) rom_1 (
    .addr(register_1_q[23:0]), .data({rom_1_data, {6{rom_1_data[6]}}}), .sel(in_3));
  decoder decoder_1 (
    .a(rom_1_data[6]), .b(rom_1_data[6]), .c(rom_1_data[6]), .d(rom_1_data[6]), .e(rom_1_data[6]),
    .f(rom_1_data[6]), .g(rom_1_data[6]), .add(out_4), .sub(out_5), .addi(out_6), .lui(out_7), .slli(out_8),
    .lw(out_9), .sw(out_10), .beq(out_11), .bne(out_12), .blt(out_13), .bge(out_14), .jal(out_15));
endmodule

module decoder (
  input  a,
  input  b,
  input  c,
  input  d,
  input  e,
  input  f,
  input  g,
  output add,
  output sub,
  output addi,
  output lui,
  output slli,
  output lw,
  output sw,
  output beq,
  output bne,
  output blt,
  output bge,
  output jal
);

  wire nand_1_out, nand_2_out, nand_3_out, nand_4_out, nand_5_out, nand_6_out, nand_7_out, nand_8_out,
       nand_9_out, nand_10_out, nand_11_out, nand_12_out, nand_13_out, nand_14_out, nand_15_out, nand_16_out,
       nand_17_out, nand_18_out, nand_19_out, nand_20_out, nand_21_out, nand_22_out, nand_23_out,
       nand_24_out, nand_25_out, nand_26_out, nand_27_out, nand_28_out, nand_29_out, nand_30_out,
       nand_31_out, nand_32_out, nand_33_out, nand_34_out, nand_35_out, nand_36_out, nand_37_out,
       nand_38_out, nand_39_out, nand_40_out, nand_41_out, nand_42_out, nand_43_out, nand_44_out,
       nand_45_out, nand_46_out, nand_47_out, nand_48_out, nand_49_out, nand_50_out;

  nand nand_1 (nand_1_out, a, a);
  nand nand_2 (nand_2_out, d, d);
  nand nand_3 (nand_3_out, e, e);
  nand nand_4 (nand_4_out, a, a);
  nand nand_5 (nand_5_out, d, d);
  nand nand_6 (nand_6_out, e, e);
  nand nand_7 (nand_7_out, a, a);
  nand nand_8 (nand_8_out, b, b);
  nand nand_9 (nand_9_out, d, d);
  nand nand_10 (nand_10_out, e, e);
  nand nand_11 (nand_11_out, a, a);
  nand nand_12 (nand_12_out, d, d);
  nand nand_13 (nand_13_out, a, a);
  nand nand_14 (nand_14_out, b, b);
  nand nand_15 (nand_15_out, d, d);
  nand nand_16 (nand_16_out, e, e);
  nand nand_17 (nand_17_out, a, a);
  nand nand_18 (nand_18_out, b, b);
  nand nand_19 (nand_19_out, c, c);
  nand nand_20 (nand_20_out, d, d);
  nand nand_21 (nand_21_out, e, e);
  nand nand_22 (nand_22_out, a, a);
  nand nand_23 (nand_23_out, c, c);
  nand nand_24 (nand_24_out, d, d);
  nand nand_25 (nand_25_out, e, e);
  nand nand_26 (nand_26_out, c, c);
  nand nand_27 (nand_27_out, d, d);
  nand nand_28 (nand_28_out, e, e);
  nand nand_29 (nand_29_out, c, c);
  nand nand_30 (nand_30_out, d, d);
  nand nand_31 (nand_31_out, e, e);
  nand nand_32 (nand_32_out, c, c);
  nand nand_33 (nand_33_out, d, d);
  nand nand_34 (nand_34_out, e, e);
  nand nand_35 (nand_35_out, c, c);
  nand nand_36 (nand_36_out, d, d);
  nand nand_37 (nand_37_out, e, e);
  nand nand_38 (nand_38_out, c, c);
  nand nand_39 (nand_39_out, nand_1_out, b, c, nand_2_out, nand_3_out, f, g);
  nand nand_40 (nand_40_out, nand_4_out, b, c, nand_5_out, nand_6_out, f, g);
  nand nand_41 (nand_41_out, nand_7_out, nand_8_out, c, nand_9_out, nand_10_out, f, g);
  nand nand_42 (nand_42_out, nand_11_out, b, c, nand_12_out, e, f, g);
  nand nand_43 (nand_43_out, nand_13_out, nand_14_out, c, nand_15_out, nand_16_out, f, g);
  nand nand_44 (nand_44_out, nand_17_out, nand_18_out, nand_19_out, nand_20_out, nand_21_out, f, g);
  nand nand_45 (nand_45_out, nand_22_out, b, nand_23_out, nand_24_out, nand_25_out, f, g);
  nand nand_46 (nand_46_out, a, b, nand_26_out, nand_27_out, nand_28_out, f, g);
  nand nand_47 (nand_47_out, a, b, nand_29_out, nand_30_out, nand_31_out, f, g);
  nand nand_48 (nand_48_out, a, b, nand_32_out, nand_33_out, nand_34_out, f, g);
  nand nand_49 (nand_49_out, a, b, nand_35_out, nand_36_out, nand_37_out, f, g);
  nand nand_50 (nand_50_out, a, b, nand_38_out, d, e, f, g);
  nand nand_51 (add, nand_39_out, nand_39_out);
  nand nand_52 (sub, nand_40_out, nand_40_out);
  nand nand_53 (addi, nand_41_out, nand_41_out);
  nand nand_54 (lui, nand_42_out, nand_42_out);
  nand nand_55 (slli, nand_43_out, nand_43_out);
  nand nand_56 (lw, nand_44_out, nand_44_out);
  nand nand_57 (sw, nand_45_out, nand_45_out);
  nand nand_58 (beq, nand_46_out, nand_46_out);
  nand nand_59 (bne, nand_47_out, nand_47_out);
  nand nand_60 (blt, nand_48_out, nand_48_out);
  nand nand_61 (bge, nand_49_out, nand_49_out);
  nand nand_62 (jal, nand_50_out, nand_50_out);
endmodule
